# Fritzing sketch designe (saved by Fritzing 0.9.3b)

parts:
  Part1 = Arduino Uno (Rev3)
  Part2 = Bluetooth HC-05 Macho
  GSM_SIM_GPSR_SMS_SIM900_SIM1 = SIM800L [package=THT]
  M1 = RioRand LM2596
  S2 = H-Bridge with L298N
  Part3 = LCD1602-I2C
  M2 = DC Motor
  M3 = DC Motor
  M4 = DC Motor
  M5 = DC Motor
  S3 = KY-026
  S4 = KY-026
  S5 = KY-026
  VCC1 = 4 x AAA Battery Mount
  DHT1 = Humidity and Temperature Sensor DHT11
  J1 = Piezo Speaker
  Mod1 = KY-019 5V Relay Module [package="Breakout board"]
  J2 = Basic Servo
  M6 = DC Motor
  D1 = Rectifier Diode [part_number=1N4001 package="300 mil [THT]"]  # not connected

nets:
  N1: Part1.A0, S4.pin4
  N2: Part1.A1, S5.pin4
  N3: Part1.A2, S3.pin1
  N4: Part1.A4/SDA, Part3.SDA
  N5: Part1.A5/SCL, Part3.SCL
  N6: Part1.D8, S2.IN2
  N7: Part1.D9_PWM, S2.IN1
  N8: Part1.D10_PWM/SS, J2.pulse
  N9: Part1.D11_PWM/MOSI, DHT1.Data-signal
  N10: Part1.D13/SCK, J1.pin2
  GND: Part1.GND, S2.GND
  N11: Part1.D0/RX, Part2.TXD
  N12: Part1.D1/TX, Part2.RXD
  N13: Part1.D2, GSM_SIM_GPSR_SMS_SIM900_SIM1.SIM_RXD
  N14: Part1.D3_PWM, GSM_SIM_GPSR_SMS_SIM900_SIM1.SIM_TXD
  N15: Part1.D4, Mod1.S
  N16: Part1.D5_PWM, S2.ENB
  N17: Part1.D6_PWM, S2.IN4
  N18: Part1.D7, S2.IN3
  N19: Part1.5V, M1.Pin_3
  N20: M1.Pin_1, VCC1.+
  N21: M1.Pin_2, VCC1.-
  N22: S2.M1-01, M4.pin_1, M5.pin_1
  N23: S2.M1-02, M4.pin_2, M5.pin_2
  N24: S2.M2-01, M2.pin_1, M3.pin_1
  N25: S2.M2-02, M2.pin_2, M3.pin_2
  N26: DHT1.GND_1, J1.pin1
  N27: Mod1.NO, M6.pin_1

notes:
  Right
  center
  left
  in-
  in+

custom parts:
  H-Bridge with L298N: h-bridge
  LCD1602-I2C: A standard character display, usually with 2x16 characters. Comes in many colors with LCM1602 IIC attached.
  KY-026: ky-026 flame sensor module
  Humidity and Temperature Sensor DHT11: Digital relative humidity & temperature sensor DHT11
  KY-019 5V Relay Module: KY-019 5V Relay module, used to control AC circuits. (Special thanks to vanepp for fixing the PCB holes and other errors)
